// Logisim project Trabalho_1_item_1_A.circ as structural Verilog: 1 circuit, main circuit main
module main (
  input  B,
  input  A,
  output S1,
  output S2
);

  nor NOR (S1, ~B, ~A);  // NOR_Gate
  and and_1 (S2, A, B);

  // Notes on the sheet:
  //   Implementar uma porta AND só com portas OR e NOT
  //   - S1 e S2 devem ter a mesma saída
endmodule
