// Logisim project Trabalho_1_item_1_B.circ as structural Verilog: 1 circuit, main circuit main
module main (
  input  A,
  input  B,
  output S1,
  output S2
);

  or or_1 (S2, A, B);
  nand nand_1 (S1, ~A, ~B);  // NAND_Gate

  // Notes on the sheet:
  //   Implementar uma porta OR apenas com portas AND e NOT
  //   - S1 e S2 devem ter a mesma saída
endmodule
