// Logisim project Trabalho_1_item_2_A.circ as structural Verilog: 1 circuit, main circuit main
module main (
  input  A,
  input  B,
  input  C,
  output T
);

  wire and_1_out, and_2_out, and_3_out;

  and and_1 (and_1_out, A, B, B);
  and and_2 (and_2_out, B, C);
  and and_3 (and_3_out, C, A);
  or or_1 (T, and_1_out, and_2_out, and_3_out);

  // Notes on the sheet:
  //   T = A.B+A.B+B.C
endmodule
