// Logisim project Trabalho_1_item_3_A.circ as structural Verilog: 1 circuit, main circuit main
module main (
  input  A,
  input  B,
  input  C,
  output T
);

  wire nand_1_out, nand_2_out, nand_3_out;

  nand nand_1 (nand_1_out, A, B);
  nand nand_2 (nand_2_out, B, C);
  nand nand_3 (nand_3_out, A, C);
  nand nand_4 (T, nand_1_out, nand_2_out, nand_3_out);

  // Notes on the sheet:
  //   T = A.B+B.C+C.A
  //   Somente com portas NAND
endmodule
