// Logisim project Trabalho_1_item_3_B.circ as structural Verilog: 1 circuit, main circuit main
module main (
  input  A,
  input  B,
  input  C,
  output S
);

  wire nand_1_out, nand_2_out, nand_3_out, nand_4_out, nand_5_out, nand_6_out, nand_7_out;

  nand nand_1 (nand_1_out, A, A);
  nand nand_2 (nand_2_out, B, B);
  nand nand_3 (nand_3_out, C, C);
  nand nand_4 (nand_4_out, nand_1_out, nand_2_out, C);
  nand nand_5 (nand_5_out, A, nand_2_out, nand_3_out);
  nand nand_6 (nand_6_out, nand_1_out, B, nand_3_out);
  nand nand_7 (nand_7_out, A, B, C);
  nand nand_8 (S, nand_4_out, nand_5_out, nand_6_out, nand_7_out);

  // Notes on the sheet:
  //   S = A'.B'.C+A'.B.C'+A.B'.C'+A.B.C
  //   - Implementar somente com portas NAND
endmodule
